// Logisim project UAL.circ as structural Verilog
module UAL (
  input  [2:0] in_1,
  input  [7:0] in_2,
  input  [7:0] in_3,
  output [7:0] out_4,
  output [3:0] Flags
);

  wire and_2_out, and_3_out, and_5_out, and_6_out, CF_minus, CF_plus, OF_minus, OF_plus;
  wire [7:0] AND, l, NOT, OR, r, tunnel, tunnel_t;

  Multiplexer #(.select(3)) multiplexer_1 (
    .in0(CF_plus), .in1(CF_minus), .in2(1'b0), .in3(1'b0), .in4(1'b0), .in5(1'b0), .in6(1'b0), .in7(1'b0),
    .out(Flags[3]), .sel(in_1));  // open: en
  assign NOT = ~in_2;  // NOT_Gate not_1, 8 bits wide
  Adder adder_1 (.a(in_2), .b(in_3), .out(tunnel), .cout(CF_plus));  // open: cin
  Subtractor subtractor_1 (.a(in_2), .b(in_3), .out(tunnel_t), .bout(CF_minus));  // open: bin
  assign OR = in_2 | in_3;  // OR_Gate or_1, 8 bits wide
  assign AND = in_2 & in_3;  // AND_Gate and_1, 8 bits wide
  Shifter shifter_1 (.in(in_2), .\dist (in_3[2:0]), .out(l));
  Shifter #(.shift("lr")) shifter_2 (.in(in_2), .\dist (in_3[2:0]), .out(r));
  and and_2 (and_2_out, in_2[7], in_3[7], ~Flags[1]);  // AND_Gate
  and and_3 (and_3_out, ~in_2[7], ~in_3[7], Flags[1]);  // AND_Gate
  or or_2 (OF_plus, and_2_out, and_3_out);
  Multiplexer #(.select(3), .width(8)) multiplexer_2 (
    .in0(tunnel), .in1(tunnel_t), .in2(OR), .in3(AND), .in4(NOT), .in5(l), .in6(r), .in7({8{1'b0}}),
    .out({Flags[1], out_4[6:0]}), .sel(in_1));  // open: en
  and and_4 (Flags[2], ~Flags[1], ~out_4[6], ~out_4[5], ~out_4[4], ~out_4[3], ~out_4[2], ~out_4[1], ~out_4[0]);  // AND_Gate
  and and_5 (and_5_out, in_2[7], ~in_3[7], Flags[1]);  // AND_Gate
  or or_3 (OF_minus, and_5_out, and_6_out);
  and and_6 (and_6_out, ~in_2[7], in_3[7], Flags[1]);  // AND_Gate
  Multiplexer #(.select(3), .enable("false")) multiplexer_3 (
    .in0(OF_plus), .in1(OF_minus), .in2(1'b0), .in3(1'b0), .in4(1'b0), .in5(1'b0), .in6(1'b0), .in7(1'b0),
    .out(Flags[0]), .sel(in_1));

  assign out_4[7] = Flags[1];

  // Other names for the same wires on the sheet: ctrlUAL[2:0] = in_1; OF = Flags[0]; OFres = Flags[1]; SF = Flags[1];
  //   ZF = Flags[2]; CF = Flags[3]; rs[7:0] = in_2; OFrs = in_2[7]; rt[7:0] = in_3; OFrt = in_3[7]

  // Notes on the sheet:
  //   Carry Flag
  //   Opérations
  //   Overflow Flag
  //   Sélection
  //   Sign Flag
  //   Zero Flag
  //   Mémo
  //   000 : addition
  //   001 : soustraction
  //   010 : OU bit-à-bit
  //   011 : ET bit-à-bit
  //   100 : NON bit-à-bit
  //   101 : décalage gauche
  //   110 : décalage droite
  //   111 : ???
  //   Flags
endmodule

module decoInstru (
  input  [3:0] in_1
);
endmodule
